# Fritzing sketch hello_lightbulb (saved by Fritzing 0.8.3b)
breadboards: 1

parts:
  R1 = Resistor [tolerance=±5% resistance=100 package=THT]
  R2 = Resistor [tolerance=±5% resistance=10k package=THT]
  BUTTON1 = Arcade Button (yellow)
  LED1 = LED - 5mm [color="Red (633nm)" package="5 mm [THT]"]
  R3 = Resistor [tolerance=±5% resistance=1k package=THT]
  Part1 = Arduino Board Ethernet

nets:
  N1: R1.Pin_0, Part1.D7
  N2: R1.Pin_1, R2.Pin_1, BUTTON1.no_name_yet#1
  N3: R2.Pin_0, LED1.cathode, Part1.GND
  N4: BUTTON1.no_name_yet#2, Part1.5V
  N5: LED1.anode, R3.Pin_1
  N6: R3.Pin_0, Part1.D6_PWM

custom parts:
  Arcade Button (yellow): Adafruit Arcade Button (yellow)
